# Fritzing sketch Clima.HackKit (saved by Fritzing 0.9.3b)
breadboards: 1

parts:
  Mod1 = Meadow F7 Micro
  S1 = Pushbutton [package="[THT]"]
  S2 = Pushbutton [package="[THT]"]
  S3 = Pushbutton [package="[THT]"]
  T1 = LM35 Temperature Sensor [package="TO92 [THT]"]
  R1 = Resistor [tolerance=±5% resistance=4.7k package=THT]
  R2 = Resistor [tolerance=±5% resistance=4.7k package=THT]
  R3 = Resistor [tolerance=±5% resistance=4.7k package=THT]

nets:
  N1: Mod1.3.3V, T1.+Vs, R1.Pin_0, R2.Pin_0, R3.Pin_0
  GND: Mod1.GND, S1.Pin_3, S1.Pin_4, S2.Pin_3, S2.Pin_4, S3.Pin_3, S3.Pin_4, T1.GND
  N2: Mod1.A0, T1.Vout
  N3: Mod1.DO2, S3.Pin_1, S3.Pin_2, R1.Pin_1
  N4: Mod1.DO3, S2.Pin_1, S2.Pin_2, R2.Pin_1
  N5: Mod1.DO4, S1.Pin_1, S1.Pin_2, R3.Pin_1
