# Fritzing sketch Clima.HackKit (saved by Fritzing 0.9.9b)
breadboards: 1

parts:
  Mod1 = Meadow F7 Micro
  S1 = Pushbutton [package="[THT]"]
  S2 = Pushbutton [package="[THT]"]
  S3 = Pushbutton [package="[THT]"]
  T1 = LM35 Temperature Sensor [package="TO92 [THT]"]

nets:
  N1: Mod1.3.3V, T1.+Vs
  GND: Mod1.GND, S1.Pin_3, S1.Pin_4, S2.Pin_3, S2.Pin_4, S3.Pin_3, S3.Pin_4, T1.GND
  N2: Mod1.A0, T1.Vout
  N3: Mod1.DO2, S3.Pin_1, S3.Pin_2
  N4: Mod1.DO3, S2.Pin_1, S2.Pin_2
  N5: Mod1.DO4, S1.Pin_1, S1.Pin_2
